# Fritzing sketch DevreSemasi (saved by Fritzing 0.9.3b)
breadboards: 1

parts:
  Parça1 = Arduino Uno (Rev3) - ICSP
  hc-sr1 = hc-sr04
  LED1 = smd LED [color="Red (633nm)" package="0603 [SMD]"]
  LED2 = smd LED [color="Red (633nm)" package="0603 [SMD]"]
  LED3 = smd LED [color="Red (633nm)" package="0603 [SMD]"]
  Parça2 = Bluetooth HC-05 Macho
  R1 = Resistor [tolerance=±5% resistance=220 package="1206 [SMD]"]
  R2 = Resistor [tolerance=±5% resistance=220 package="1206 [SMD]"]
  M1 = DC Motor
  R3 = Resistor [tolerance=±5% resistance=220 package="1206 [SMD]"]
  R4 = Resistor [tolerance=±5% resistance=330 package="2010 [SMD]"]
  Q1 = TRANSISTOR_NPN [package=to-92]
  R5 = Resistor [tolerance=±5% resistance=330 package="0805 [SMD]"]
  J1 = Piezo Speaker
  R6 = Photocell (LDR) [package=THT]
  R7 = Resistor [tolerance=±5% resistance=10k package="2010 [SMD]"]
  R8 = Resistor [tolerance=±5% resistance=220 package="2010 [SMD]"]
  R9 = Resistor [tolerance=±5% resistance=220 package="2010 [SMD]"]
  U1 = GAS_SENSOR [package=mq-3]
  LED4 = smd LED [color="Red (633nm)" package="0805 [SMD]"]
  LED5 = smd LED [color="Red (633nm)" package="0805 [SMD]"]

nets:
  N1: Parça1.A0, U1.A0
  N2: Parça1.A1, R6.pin_0, R7.Pin_1
  N3: Parça1.ICSP_MISO, Parça1.D12/MISO, R2.Pin_1
  N4: Parça1.D9_PWM, R5.Pin_1
  N5: Parça1.D10_PWM/SS, R3.Pin_1
  N6: Parça1.D11_PWM/MOSI, R4.Pin_1
  N7: Parça1.D13/SCK, R1.Pin_1
  N8: Parça1.D0/RX, Parça2.TXD
  N9: Parça1.D1/TX, Parça2.RXD
  N10: Parça1.D4, R8.Pin_1
  N11: Parça1.D5_PWM, R9.Pin_1
  N12: Parça1.D6_PWM, hc-sr1.Echo
  N13: Parça1.D7, hc-sr1.Trig
  N14: Parça1.3V3, M1.pin_1
  VCC: Parça1.5V, hc-sr1.VCC, Parça2.VCC, U1.VCC
  GND: Parça1.GND, hc-sr1.GND, LED1.cathode, LED2.cathode, LED3.cathode, Parça2.GND, Q1.C, R6.pin_1, R7.Pin_0, R8.Pin_0, U1.GND, LED4.cathode, LED5.anode
  N15: LED1.anode, R1.Pin_0
  N16: LED2.anode, R2.Pin_0
  N17: LED3.anode, R3.Pin_0
  N18: M1.pin_2, Q1.E
  N19: R4.Pin_0, Q1.B
  N20: R5.Pin_0, J1.pin2
  N21: R9.Pin_0, LED4.anode

custom parts:
  GAS_SENSOR: MQ-3 alcohol gas sensor . FP not tested. SEN-08880.
